// Digital circuit And.dig as structural Verilog
module And (
  input  A,
  input  B,
  output Out
);

  wire nand_1_out;

  nand nand_1 (nand_1_out, A, B);
  nand nand_2 (Out, nand_1_out, nand_1_out);

  // Notes on the sheet:
  //   And Gate
endmodule
