// Digital circuit Or16.dig as structural Verilog
module Or16 (
  input  [7:0] In,
  output Out
);

  wire or_1_out, or_2_out, or_3_out, or_4_out, or_5_out, or_6_out;

  or or_1 (or_1_out, In[0], In[1]);
  or or_2 (or_2_out, In[2], In[3]);
  or or_3 (or_3_out, In[4], In[5]);
  or or_4 (or_4_out, In[6], In[7]);
  or or_5 (or_5_out, or_1_out, or_2_out);
  or or_6 (or_6_out, or_3_out, or_4_out);
  or or_7 (Out, or_5_out, or_6_out);

  // Notes on the sheet:
  //   8-Way Or Gate
endmodule
