// Digital circuit ALU.dig as structural Verilog
module ALU (
  input  [15:0] A,
  input  [15:0] B,
  input  zx,
  input  nx,
  input  zy,
  input  ny,
  input  f,
  input  no,
  output [15:0] Out,
  output ng,
  output zr
);

  wire [15:0] adder16_1_sum, and_1_out, multiplexer_1_out, multiplexer_2_out, multiplexer_3_out,
       multiplexer_4_out, multiplexer_5_out, not_1_out, not_2_out, not_3_out;

  Multiplexer #(.Bits(16)) multiplexer_1 (.sel(zx), .in_0(A), .in_1({16{1'b0}}), .out(multiplexer_1_out));
  assign not_1_out = ~multiplexer_1_out;  // Not not_1, 16 bits wide
  Multiplexer #(.Bits(16)) multiplexer_2 (
    .sel(nx), .in_0(multiplexer_1_out), .in_1(not_1_out), .out(multiplexer_2_out));
  Multiplexer #(.Bits(16)) multiplexer_3 (.sel(zy), .in_0(B), .in_1({16{1'b0}}), .out(multiplexer_3_out));
  assign not_2_out = ~multiplexer_3_out;  // Not not_2, 16 bits wide
  Multiplexer #(.Bits(16)) multiplexer_4 (
    .sel(ny), .in_0(multiplexer_3_out), .in_1(not_2_out), .out(multiplexer_4_out));
  assign and_1_out = multiplexer_2_out & multiplexer_4_out;  // And and_1, 16 bits wide
  Adder16 adder16_1 (.A(multiplexer_2_out), .B(multiplexer_4_out), .Sum(adder16_1_sum));
  Multiplexer #(.Bits(16)) multiplexer_5 (.sel(f), .in_0(and_1_out), .in_1(adder16_1_sum), .out(multiplexer_5_out));
  Multiplexer #(.Bits(16)) multiplexer_6 (.sel(no), .in_0(multiplexer_5_out), .in_1(not_3_out), .out({ng, Out[14:0]}));
  assign not_3_out = ~multiplexer_5_out;  // Not not_3, 16 bits wide
  or or_1 (zr, Out[0], Out[1], Out[2], Out[3], Out[4], Out[5], Out[6], Out[7], Out[8], Out[9], Out[10], Out[11], Out[12], Out[13], Out[14], ng);

  assign Out[15] = ng;

  // Notes on the sheet:
  //   zx: If zx == 1, x = 0
  //   nx: If nx == 1, x = !x
  //   zy: if zy == 1, y = 0
  //   ny: if ny = 1, y = !y
  //   f: if f == 1, out = x+y
  //   else out == x & y
  //   no: if no == 1, out = !out
  //   Arithmetic Logic Unit (ALU)
  //   Control Bits
  //   Flags
endmodule
