// Digital circuit Adder.dig as structural Verilog
module Adder (
  input  [15:0] A,
  input  [15:0] B
);

  wire halfadder_1_p3, halfadder_1_p4;

  // HalfAdder halfadder_1: pin names not known; wires that end beside it: A, B, halfadder_1_p3, halfadder_1_p4
  // FullAdder fulladder_1: pin names not known; wires that end beside it: halfadder_1_p3, halfadder_1_p4

  // Notes on the sheet:
  //   Adder (16-bit)
endmodule
