// Digital circuit Adder4.dig as structural Verilog
module Adder4 (
  input  [3:0] A,
  input  [3:0] B,
  output [3:0] Sum
);

  wire fulladder_1_carry, fulladder_2_carry, halfadder_1_carry;

  HalfAdder halfadder_1 (.A(A[0]), .B(B[0]), .Sum(Sum[0]), .Carry(halfadder_1_carry));
  FullAdder fulladder_1 (.A(A[1]), .B(B[1]), .C(halfadder_1_carry), .Carry(fulladder_1_carry), .Sum(Sum[1]));
  FullAdder fulladder_2 (.A(A[2]), .B(B[2]), .C(fulladder_1_carry), .Carry(fulladder_2_carry), .Sum(Sum[2]));
  FullAdder fulladder_3 (.A(A[3]), .B(B[3]), .C(fulladder_2_carry), .Sum(Sum[3]));  // open: Carry

  // Notes on the sheet:
  //   Adder (4-bit)
endmodule
