// Digital circuit Bit.dig as structural Verilog
module Bit (
  input  In,
  input  Load,
  input  Clock,
  output Out
);

  wire multiplexer_1_out;

  Multiplexer multiplexer_1 (.sel(Load), .in_0(In), .in_1(Out), .out(multiplexer_1_out));
  D_FF d_ff_1 (.D(multiplexer_1_out), .C(Clock), .Q(Out));  // open: nQ

  // Notes on the sheet:
  //   Bit (1-bit Register)
endmodule
