// Digital circuit Adder16.dig as structural Verilog
module Adder16 (
  input  [15:0] A,
  input  [15:0] B,
  output [15:0] Sum
);

  wire fulladder_1_carry, fulladder_2_carry, fulladder_3_carry, fulladder_4_carry, fulladder_5_carry,
       fulladder_6_carry, fulladder_7_carry, fulladder_8_carry, fulladder_9_carry, fulladder_10_carry,
       fulladder_11_carry, fulladder_12_carry, fulladder_13_carry, fulladder_14_carry, halfadder_1_carry;

  HalfAdder halfadder_1 (.A(A[0]), .B(B[0]), .Sum(Sum[0]), .Carry(halfadder_1_carry));
  FullAdder fulladder_1 (.A(A[1]), .B(B[1]), .C(halfadder_1_carry), .Carry(fulladder_1_carry), .Sum(Sum[1]));
  FullAdder fulladder_2 (.A(A[2]), .B(B[2]), .C(fulladder_1_carry), .Carry(fulladder_2_carry), .Sum(Sum[2]));
  FullAdder fulladder_3 (.A(A[3]), .B(B[3]), .C(fulladder_2_carry), .Carry(fulladder_3_carry), .Sum(Sum[3]));
  FullAdder fulladder_4 (.A(A[4]), .B(B[4]), .C(fulladder_3_carry), .Carry(fulladder_4_carry), .Sum(Sum[4]));
  FullAdder fulladder_5 (.A(A[5]), .B(B[5]), .C(fulladder_4_carry), .Carry(fulladder_5_carry), .Sum(Sum[5]));
  FullAdder fulladder_6 (.A(A[6]), .B(B[6]), .C(fulladder_5_carry), .Carry(fulladder_6_carry), .Sum(Sum[6]));
  FullAdder fulladder_7 (.A(A[7]), .B(B[7]), .C(fulladder_6_carry), .Carry(fulladder_7_carry), .Sum(Sum[7]));
  FullAdder fulladder_8 (.A(A[8]), .B(B[8]), .C(fulladder_7_carry), .Carry(fulladder_8_carry), .Sum(Sum[8]));
  FullAdder fulladder_9 (.A(A[9]), .B(B[9]), .C(fulladder_8_carry), .Carry(fulladder_9_carry), .Sum(Sum[9]));
  FullAdder fulladder_10 (.A(A[10]), .B(B[10]), .C(fulladder_9_carry), .Carry(fulladder_10_carry), .Sum(Sum[10]));
  FullAdder fulladder_11 (.A(A[11]), .B(B[11]), .C(fulladder_10_carry), .Carry(fulladder_11_carry), .Sum(Sum[11]));
  FullAdder fulladder_12 (.A(A[12]), .B(B[12]), .C(fulladder_11_carry), .Carry(fulladder_12_carry), .Sum(Sum[12]));
  FullAdder fulladder_13 (.A(A[13]), .B(B[13]), .C(fulladder_12_carry), .Carry(fulladder_13_carry), .Sum(Sum[13]));
  FullAdder fulladder_14 (.A(A[14]), .B(B[14]), .C(fulladder_13_carry), .Carry(fulladder_14_carry), .Sum(Sum[14]));
  FullAdder fulladder_15 (.A(A[15]), .B(B[15]), .C(fulladder_14_carry), .Sum(Sum[15]));  // open: Carry

  // Notes on the sheet:
  //   Adder (16-bit)
endmodule
