// Digital circuit Bit.dig as structural Verilog
module Bit (
  input  In,
  input  Load,
  input  Clock,
  output Out
);

  wire d_ff_1_nq, multiplexer_1_out;

  Multiplexer multiplexer_1 (.sel(Load), .in_0(d_ff_1_nq), .in_1(In), .out(multiplexer_1_out));
  D_FF d_ff_1 (.D(multiplexer_1_out), .C(Clock), .Q(Out), .nQ(d_ff_1_nq));

  // Notes on the sheet:
  //   Bit (1-bit Register)
endmodule
