// Digital circuit CPU.dig as structural Verilog
module CPU (
  input  [15:0] inM,
  input  clk,
  input  reset,
  input  [15:0] Instruction,
  output [15:0] outM,
  output writeM,
  output [14:0] addressM,
  output [14:0] pc
);

  wire and_1_out, and_2_out, and_3_out, cAorM, cDestA, cDestD, cF, cJEQ, cJGT, cJLT, cNO, cNX, cNY, cZX, cZY,
       LoadA, Neg, not_1_out, not_2_out, or_2_out, Pos, Zero;
  wire [14:13] multiplexer_1_out;
  wire [15:0] DRegOut, multiplexer_3_out, YIn;
  wire [15:15] ARegOut, pc_1_out;

  Multiplexer #(.Bits(16)) multiplexer_1 (
    .sel(Instruction[15]), .in_0({16{1'b0}}), .in_1(Instruction),
    .out({Instruction[15], multiplexer_1_out, cAorM, cZX, cNX, cZY, cNY, cF, cNO, cDestA, cDestD, writeM, cJLT, cJEQ, cJGT}));
  or or_1 (LoadA, Instruction[15], cDestA);
  Multiplexer #(.Bits(16)) multiplexer_2 (.sel(Instruction[15]), .in_0({ARegOut[15], addressM}), .in_1(inM), .out(YIn));
  Multiplexer #(.Bits(16)) multiplexer_3 (.sel(cDestA), .in_0(Instruction), .in_1(outM), .out(multiplexer_3_out));
  ALU alu_1 (
    .A(DRegOut), .B(YIn), .zx(cZX), .nx(cNX), .zy(cZY), .ny(cNY), .f(cF), .no(cNO), .Out(outM), .ng(Neg),
    .zr(Zero));
  and and_1 (and_1_out, cJLT, Neg);
  and and_2 (and_2_out, cJEQ, Zero);
  and and_3 (and_3_out, cJGT, Pos);
  Register A_Register (.In(multiplexer_3_out), .Load(LoadA), .Clock(clk), .Out({ARegOut[15], addressM}));
  not not_1 (not_1_out, Neg);
  not not_2 (not_2_out, Zero);
  and and_4 (Pos, not_1_out, not_2_out);
  or or_2 (or_2_out, and_1_out, and_2_out, and_3_out);
  Register D_Register (.In(outM), .Load(cDestD), .Clock(clk), .Out(DRegOut));
  PC pc_1 (
    .in({ARegOut[15], addressM}), .load(or_2_out), .reset(reset), .Clock(clk), .inc(1'b1),
    .out({pc_1_out[15], pc}));

  // Other names for the same wires on the sheet: cDestM = writeM; AInput[15:0] = Instruction; cType = Instruction[15];
  //   ALUOut[15:0] = outM; ARegOut[14:0] = addressM; Clock = clk

  // Notes on the sheet:
  //   CPU
endmodule
