// Digital circuit DMux.dig as structural Verilog
module DMux (
  input  In,
  input  Sel,
  output A,
  output B
);

  wire not_1_out;

  not not_1 (not_1_out, Sel);
  and and_1 (A, In, not_1_out);
  and and_2 (B, In, Sel);

  // Notes on the sheet:
  //   Demultiplexer (DMux) Gate
endmodule
