// Digital circuit Incrementer.dig as structural Verilog
module Incrementer (
  input  [15:0] A,
  output [15:0] Sum
);

  Adder16 adder16_1 (.A(A), .B(16'h1), .Sum(Sum));

  // Notes on the sheet:
  //   *Inc is always a
  //   16-bit binary 1
  //   Incrementer
endmodule
