// Digital circuit PC.dig as structural Verilog
module PC (
  input  [15:0] in,
  input  load,
  input  reset,
  input  Clock,
  input  inc,
  output [15:0] out
);

  wire [15:0] multiplexer_1_out, multiplexer_2_out, multiplexer_3_out, not_1_out, register_1_out;

  Multiplexer #(.Bits(16)) multiplexer_1 (.sel(load), .in_0(multiplexer_3_out), .in_1(in), .out(multiplexer_1_out));
  assign not_1_out = ~16'h1;  // Not not_1, 16 bits wide
  Multiplexer #(.Bits(16)) multiplexer_2 (
    .sel(reset), .in_0(multiplexer_1_out), .in_1(not_1_out), .out(multiplexer_2_out));
  Register register_1 (.In(multiplexer_2_out), .Load(1'b1), .Clock(Clock), .Out(register_1_out));
  Incrementer incrementer_1 (.A(register_1_out), .Sum(out));
  Multiplexer #(.Bits(16)) multiplexer_3 (.sel(inc), .in_0(register_1_out), .in_1(out), .out(multiplexer_3_out));

  // Notes on the sheet:
  //   Program Counter (PC)
endmodule
