// Digital circuit RAM8.dig as structural Verilog
module RAM8 (
  input  [2:0] Address,
  input  Load,
  input  Clock,
  input  [15:0] In,
  output [15:0] Out
);

  wire demultiplexer_1_out_0, demultiplexer_1_out_1, demultiplexer_1_out_2, demultiplexer_1_out_3,
       demultiplexer_1_out_4, demultiplexer_1_out_5, demultiplexer_1_out_6, demultiplexer_1_out_7;
  wire [15:0] register_1_out, register_2_out, register_3_out, register_4_out, register_5_out, register_6_out,
       register_7_out, register_8_out;

  Demultiplexer #(.Selector_Bits(3)) demultiplexer_1 (
    .sel(Address), .in(Load), .out_0(demultiplexer_1_out_0), .out_1(demultiplexer_1_out_1),
    .out_2(demultiplexer_1_out_2), .out_3(demultiplexer_1_out_3), .out_4(demultiplexer_1_out_4),
    .out_5(demultiplexer_1_out_5), .out_6(demultiplexer_1_out_6), .out_7(demultiplexer_1_out_7));
  Register register_1 (.In(In), .Load(demultiplexer_1_out_0), .Clock(Clock), .Out(register_1_out));
  Register register_2 (.In(In), .Load(demultiplexer_1_out_1), .Clock(Clock), .Out(register_2_out));
  Register register_3 (.In(In), .Load(demultiplexer_1_out_2), .Clock(Clock), .Out(register_3_out));
  Register register_4 (.In(In), .Load(demultiplexer_1_out_3), .Clock(Clock), .Out(register_4_out));
  Register register_5 (.In(In), .Load(demultiplexer_1_out_4), .Clock(Clock), .Out(register_5_out));
  Register register_6 (.In(In), .Load(demultiplexer_1_out_5), .Clock(Clock), .Out(register_6_out));
  Register register_7 (.In(In), .Load(demultiplexer_1_out_6), .Clock(Clock), .Out(register_7_out));
  Register register_8 (.In(In), .Load(demultiplexer_1_out_7), .Clock(Clock), .Out(register_8_out));
  Multiplexer #(.Bits(16), .Selector_Bits(3)) multiplexer_1 (
    .sel(Address), .in_0(register_1_out), .in_1(register_2_out), .in_2(register_3_out),
    .in_3(register_4_out), .in_4(register_5_out), .in_5(register_6_out), .in_6(register_7_out),
    .in_7(register_8_out), .out(Out));

  // Notes on the sheet:
  //   RAM8
endmodule
