// Digital circuit 4WayDMux.dig as structural Verilog
module _4WayDMux (
  input  In,
  input  [1:0] Sel,
  output A,
  output B,
  output C,
  output D
);

  wire demultiplexer_1_out_0, demultiplexer_1_out_1;

  Demultiplexer demultiplexer_1 (.sel(Sel[1]), .in(In), .out_0(demultiplexer_1_out_0), .out_1(demultiplexer_1_out_1));
  Demultiplexer demultiplexer_2 (.sel(Sel[0]), .in(demultiplexer_1_out_0), .out_0(A), .out_1(B));
  Demultiplexer demultiplexer_3 (.sel(Sel[0]), .in(demultiplexer_1_out_1), .out_0(C), .out_1(D));

  // Notes on the sheet:
  //   4-Way DMux Gate
endmodule
