// Digital circuit HalfAdder.dig as structural Verilog
module HalfAdder (
  input  A,
  input  B,
  output Sum,
  output Carry
);

  xor xor_1 (Sum, A, B);
  and and_1 (Carry, A, B);

  // Notes on the sheet:
  //   HalfAdder
endmodule
