// Digital circuit Xor.dig as structural Verilog
module Xor (
  input  A,
  input  B,
  output Out
);

  wire nand_1_out, nand_2_out, not_1_out, not_2_out;

  not not_1 (not_1_out, B);
  not not_2 (not_2_out, A);
  nand nand_1 (nand_1_out, A, not_1_out);
  nand nand_2 (nand_2_out, not_2_out, B);
  nand nand_3 (Out, nand_1_out, nand_2_out);

  // Notes on the sheet:
  //   XOR Gate
endmodule
