// Digital circuit And16.dig as structural Verilog
module And16 (
  input  [1:0] A,
  input  [1:0] B,
  output [1:0] out_3
);

  assign out_3 = A & B;  // And and_1, 2 bits wide

  // Notes on the sheet:
  //   And16 Gate
endmodule
