// Digital circuit Mux.dig as structural Verilog
module Mux (
  input  A,
  input  B,
  input  Sel,
  output Out
);

  wire and_1_out, and_2_out, not_1_out;

  not not_1 (not_1_out, Sel);
  and and_1 (and_1_out, A, not_1_out);
  and and_2 (and_2_out, B, Sel);
  xor xor_1 (Out, and_1_out, and_2_out);

  // Notes on the sheet:
  //   Multiplexer (MUX) Gate
endmodule
