// Digital circuit Not16.dig as structural Verilog
module Not16 (
  input  [1:0] In,
  output [1:0] Out
);

  not not_1 (Out[0], In[0]);
  not not_2 (Out[1], In[1]);

  // Notes on the sheet:
  //   Not16 Gate
  //   0..15
endmodule
