// Digital circuit Or.dig as structural Verilog
module Or (
  input  A,
  input  B,
  output Out
);

  wire not_1_out, not_2_out;

  not not_1 (not_1_out, A);
  not not_2 (not_2_out, B);
  nand nand_1 (Out, not_1_out, not_2_out);

  // Notes on the sheet:
  //   Or Gate
endmodule
